// Digital circuit CPU.dig as structural Verilog
module CPU (
  input  CLOCK,
  output [7:0] HI,
  output [7:0] LO
);

  wire alu_8_bit_1_zero, AluSrc, and_1_out, and_2_out, BEQ_eq, Branch, C, JAL_eq, Jump, LUI_eq, MemRead,
       MemtoReg, MemWrite, or_1_out, RegDst, RegWrite, WRITELOHI;
  wire [2:0] Instruction_Memory_d_2, Instruction_Memory_d_3, multiplexer_1_out, multiplexer_2_out;
  wire [3:0] AluOp;
  wire [5:0] Instruction_Memory_d;
  wire [7:0] add_1_s, add_2_s, add_3_s, alu_8_bit_1_high, alu_8_bit_1_s, barrelshifter_1_out,
       barrelshifter_2_out, bitextender_1_out, Data_Memory_d, multiplexer_3_out, multiplexer_4_out,
       multiplexer_5_out, multiplexer_6_out, multiplexer_7_out, multiplexer_8_out, PC, Registers_da,
       Registers_db;
  wire [15:12] Instruction_Memory_d_4;

  Button button_1 (.out(C));
  Register #(.Bits(8), .isProgramCounter("true")) u_PC (.D(multiplexer_4_out), .C(C), .en(C), .Q(PC));
  Add #(.Bits(8)) add_1 (.a(8'h4), .b(PC), .c_i(1'b0), .s(add_1_s));  // open: c_o
  ROM #(.AddrBits(8), .isProgramMemory("true"), .Bits(16)) Instruction_Memory (
    .A(PC), .sel(1'b1),
    .D({Instruction_Memory_d_4, Instruction_Memory_d_3, Instruction_Memory_d_2, Instruction_Memory_d}));
  LookUpTable #(.Bits(13)) CONTROLLER (
    .in0(Instruction_Memory_d[0]), .in1(Instruction_Memory_d[1]), .in2(Instruction_Memory_d[2]),
    .in3(Instruction_Memory_d_4[12]), .in4(Instruction_Memory_d_4[13]), .in5(Instruction_Memory_d_4[14]),
    .in6(Instruction_Memory_d_4[15]),
    .out({WRITELOHI, MemRead, AluOp, Jump, Branch, MemWrite, RegWrite, MemtoReg, AluSrc, RegDst}));
  Multiplexer #(.Bits(3)) multiplexer_1 (
    .sel(RegDst), .in_0(Instruction_Memory_d[5:3]), .in_1(Instruction_Memory_d_2), .out(multiplexer_1_out));
  BitExtender #(.inputBits(6), .outputBits(8)) bitextender_1 (.in(Instruction_Memory_d), .out(bitextender_1_out));
  Comparator #(.Bits(4)) LUI (.a(Instruction_Memory_d_4), .b(4'b1101), .eq(LUI_eq));  // open: gt, lt
  BarrelShifter #(.Bits(8)) barrelshifter_1 (.in(bitextender_1_out), .shift(4'b0010), .out(barrelshifter_1_out));
  Add #(.Bits(8)) add_2 (.a(add_1_s), .b(barrelshifter_1_out), .c_i(1'b0), .s(add_2_s));  // open: c_o
  Comparator #(.Bits(4)) JAL (.a(Instruction_Memory_d_4), .b(4'b0100), .eq(JAL_eq));  // open: gt, lt
  Multiplexer #(.Bits(3)) multiplexer_2 (
    .sel(JAL_eq), .in_0(multiplexer_1_out), .in_1(3'b111), .out(multiplexer_2_out));
  Multiplexer #(.Bits(8)) multiplexer_3 (.sel(and_1_out), .in_0(add_1_s), .in_1(add_2_s), .out(multiplexer_3_out));
  BarrelShifter #(.Bits(8)) barrelshifter_2 (.in(bitextender_1_out), .shift(4'b0100), .out(barrelshifter_2_out));
  Multiplexer #(.Bits(8)) multiplexer_4 (
    .sel(Jump), .in_0(multiplexer_3_out), .in_1({Instruction_Memory_d_2[1:0], Instruction_Memory_d}),
    .out(multiplexer_4_out));
  Comparator #(.Bits(4)) BEQ (.a(4'b1000), .b(Instruction_Memory_d_4), .eq(BEQ_eq));  // open: gt, lt
  RegisterFile #(.AddrBits(3), .Bits(8)) Registers (
    .Din(multiplexer_7_out), .we(RegWrite), .Rw(multiplexer_2_out), .C(C), .Ra(Instruction_Memory_d_3),
    .Rb(Instruction_Memory_d_2), .Da(Registers_da), .Db(Registers_db));
  Multiplexer #(.Bits(8)) multiplexer_5 (
    .sel(LUI_eq), .in_0(bitextender_1_out), .in_1(barrelshifter_2_out), .out(multiplexer_5_out));
  and and_1 (and_1_out, or_1_out, Branch);
  or or_1 (or_1_out, BEQ_eq, alu_8_bit_1_zero);
  Multiplexer #(.Bits(8)) multiplexer_6 (
    .sel(AluSrc), .in_0(Registers_db), .in_1(multiplexer_5_out), .out(multiplexer_6_out));
  ALU_8_BIT alu_8_bit_1 (
    .ALUop(AluOp), .S(alu_8_bit_1_s), .A(Registers_da), .B(multiplexer_6_out),
    .SHAMT(Instruction_Memory_d_3), .HIGH(alu_8_bit_1_high), .ZERO(alu_8_bit_1_zero));
  and and_2 (and_2_out, 1'b1, WRITELOHI);
  Register #(.Bits(8)) u_LO (.D(alu_8_bit_1_s), .C(C), .en(and_2_out), .Q(LO));
  Register #(.Bits(8)) u_HI (.D(alu_8_bit_1_high), .C(C), .en(and_2_out), .Q(HI));
  RAMDualPort #(.AddrBits(8), .Bits(8)) Data_Memory (
    .A(alu_8_bit_1_s), .Din(Registers_db), .str(MemWrite), .C(C), .ld(MemRead), .D(Data_Memory_d));
  Multiplexer #(.Bits(8)) multiplexer_7 (
    .sel(JAL_eq), .in_0(multiplexer_8_out), .in_1(add_3_s), .out(multiplexer_7_out));
  Multiplexer #(.Bits(8)) multiplexer_8 (
    .sel(MemtoReg), .in_0(alu_8_bit_1_s), .in_1(Data_Memory_d), .out(multiplexer_8_out));
  Add #(.Bits(8)) add_3 (.a(PC), .b(8'h8), .c_i(1'b0), .s(add_3_s));  // open: c_o

  // Notes on the sheet:
  //   contents of Instruction_Memory (hex, n*v repeats v):
  //   7045
  //   ADDR
  //   OPCODE
  //   8 bits of Address
  //   IMM
  //   RT
  //   RS
  //   FUNCT
  //   RD
  //   contents of CONTROLLER (hex, n*v repeats v):
  //   0,589,609,689,0,0,0,8,8,88,88,388,408,1200,1200,1280,1300,488
  //   ,708,208,508,0,0,0,16*40,16*a0,16*b,16*70b,8*38b,16*40b,8*80f
  //   ,8*12
  //   RegDst
  //   Jump
  //   Branch
  //   ALUSrc
  //   WriteLOHI
  //   MemtoReg
endmodule
